// Logisim project ProyectoFinalizado.circ as structural Verilog: 1 circuit, main circuit main
module main (
  input  [2:0] \Selección ,
  input  [3:0] Registro_A,
  input  [3:0] Registro_B,
  output [3:0] out_4
);

  wire button_1_out, button_2_out, dip_7408_1_p1, dip_74283_1_p1, multiplexer_2_out, register_2_q, undriven;
  wire [3:0] adder_1_out, dip_7408_1_p10, dip_74283_1_p8, multiplexer_1_out, shifter_1_out, xor_1_out;

  assign xor_1_out = {4{\Selección [2]}} ^ Registro_B;  // XOR_Gate xor_1, 4 bits wide
  Adder #(.width(4)) adder_1 (.a(xor_1_out), .b({3'b000, \Selección [2]}), .out(adder_1_out));  // open: cin, cout
  Shifter #(.width(4)) shifter_1 (.in(Registro_A), .\dist (2'b11), .out(shifter_1_out));
  // DIP_7408 dip_7408_1: pin names not known; wires that end beside it: dip_7408_1_p1, dip_7408_1_p1, dip_7408_1_p10[2], dip_7408_1_p10[1], Registro_A[2], adder_1_out[1], adder_1_out[2], Registro_A[1], dip_7408_1_p10[3], dip_7408_1_p10[0], Registro_A[3], adder_1_out[0], adder_1_out[3], Registro_A[0]
  // DIP_74283 dip_74283_1: pin names not known; wires that end beside it: dip_74283_1_p1, 1'b0, dip_74283_1_p8[3], adder_1_out[0], Registro_A[3], Registro_A[0], adder_1_out[3], dip_74283_1_p8[0], dip_74283_1_p8[2], adder_1_out[1], Registro_A[2], Registro_A[1], adder_1_out[2], dip_74283_1_p8[1]
  Multiplexer #(.select(2), .width(4)) multiplexer_1 (
    .in0(dip_7408_1_p10), .in1(shifter_1_out), .in2(dip_74283_1_p8), .out(multiplexer_1_out),
    .sel(\Selección [1:0]));  // open: in3, en
  Multiplexer #(.select(2)) multiplexer_2 (
    .in0(1'b0), .in1(1'b0), .in2(dip_74283_1_p1), .in3(1'b0), .out(multiplexer_2_out), .sel(\Selección [1:0]));  // open: en
  Button button_1 (.out(button_1_out));
  Button button_2 (.out(button_2_out));
  Register #(.width(4)) register_1 (
    .D(multiplexer_1_out), .Q(out_4), .clk(button_2_out), .clr(button_1_out));  // open: en
  Register #(.width(1), .trigger("high")) register_2 (
    .D(multiplexer_2_out), .Q(register_2_q), .clk(button_2_out), .clr(button_1_out));  // open: en
  LED led_1 (.in(register_2_q));
  LED led_2 (.in(undriven));

  // Notes on the sheet:
  //   A AND B
  //   -00
  //   A << 0
  //   -01
  //   A + B
  //   -10
  //   Si Bit de Selección de mayor peso = 0;
  //   B se queda igual
  //   Si Bit de Selección de mayor peso = 1;
  //   B se pasa a Ca2
  //   Start ejecuta la orden
  //   Reset resetea las memorias
  //   Start
  //   Reset
  //   Memoria de C
  //   Memoria de Carry de C
  //   Registro C
  //   Carry
  //   Overflow
endmodule
